# Fritzing sketch Aufbau Hardware (saved by Fritzing 0.9.3b)

parts:
  Raspberry_Pi_Zero1 = Raspberry Pi Zero
  Bauteil1 = RFID-RC522-v2
  Bauteil2 = Adafruit VL53L0X Time of Flight Distance Sensor [part_number="Adafruit #3317"]

nets:
  3V3: Raspberry_Pi_Zero1.3v3, Raspberry_Pi_Zero1.3V3, Bauteil1.3.3V, Bauteil2.VIN
  N1: Raspberry_Pi_Zero1.GPIO2, Bauteil2.SCL
  N2: Raspberry_Pi_Zero1.GPIO3, Bauteil2.SDA
  N3: Raspberry_Pi_Zero1.GPIO10, Bauteil1.MOSI
  N4: Raspberry_Pi_Zero1.GPIO9, Bauteil1.MISO
  N5: Raspberry_Pi_Zero1.GPIO11, Bauteil1.SCK
  N6: Raspberry_Pi_Zero1.GPIO8, Bauteil1.SDA
  N7: Raspberry_Pi_Zero1.GPIO25, Bauteil1.RST
  GND: Raspberry_Pi_Zero1.GND, Bauteil1.IRQ, Bauteil1.GND, Bauteil2.GND

custom parts:
  RFID-RC522-v2: A simple China made RFID-RC522 Reader; do check the pin labels, as this is a MFRC522 based clone.
  Adafruit VL53L0X Time of Flight Distance Sensor: The VL53L0X is a Time of Flight distance sensor like no other you've used! The sensor contains a very tiny invisible laser source, and a matching sensor. The VL53L0X can detect the "time of flight", or how long the light has taken to bounce back to the sensor. Since it uses a very narrow light source, it is good for determining distance of only the surface directly in front of it. Unlike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
